# Fritzing sketch control_unit_pinout (saved by Fritzing 1.0.1rc)

parts:
  J1 = STM32 Nucleo boards
  Raspberry_Pi1 = Raspberry Pi 2
  M1 = RioRand LM2596
  M2 = RioRand LM2596
  M3 = fc-51 [package=THT]
  M4 = fc-51 [package=THT]
  M5 = fc-51 [package=THT]
  M6 = DC Motor [voltage_(max)=6V voltage_(min)=3V]
  Tank_2_Solenoids = KY-019 5V Relay Module [package="Breakout board"]
  Tank_1_Solenoids = KY-019 5V Relay Module [package="Breakout board"]
  Fire_Ext_Extnd = KY-019 5V Relay Module [package="Breakout board"]
  Fire_Ext_Retr = KY-019 5V Relay Module [package="Breakout board"]
  SSR1 = SSR-40DD Solid State Relay (40A, w/ Heatsink) [part_number=SSR-40DD package="Screw Terminal, Heatsink Mount"]
  Tank_1_Heater = Inductor [package="0603 [SMD]"]
  SSR2 = SSR-40DD Solid State Relay (40A, w/ Heatsink) [part_number=SSR-40DD package="Screw Terminal, Heatsink Mount"]
  Tank_2 = Inductor [package="0603 [SMD]"]
  SSR3 = SSR-40DD Solid State Relay (40A, w/ Heatsink) [part_number=SSR-40DD package="Screw Terminal, Heatsink Mount"]
  Nozzle_Heater = Inductor [package="0603 [SMD]"]
  Tank_1_Upper_Solenoid = Solenoid
  Tank_2_Upper_Solenoid = Solenoid
  Tank_1_Lower_Solenoid = Solenoid
  Tank_2_Lower_Solenoid = Solenoid
  SSR4 = SSR-40DD Solid State Relay (40A, w/ Heatsink) [part_number=SSR-40DD package="Screw Terminal, Heatsink Mount"]
  PSU1 = 12V Power Supply (4x + / 4x -) [package="Screw Terminal Block"]
  GND1 = Ground Point [package="Reference symbol"]
  GND2 = Ground Point [package="Reference symbol"]
  GND3 = Ground Point [package="Reference symbol"]
  A_______B = Linear Actuator (2-wire DC) [package="2-wire, reversible DC"]
  GND5 = Ground Point [package="Reference symbol"]
  PWR1 = 3.3V Power Point [package="Reference symbol"]
  F1 = FUSE [package=fuse_5mm]
  GND9 = Ground Point [package="Reference symbol"]
  PWR5 = 12V Power Point [package="Reference symbol"]
  GND10 = Ground Point [package="Reference symbol"]
  PWR6 = 3.3V Power Point [package="Reference symbol"]
  GND11 = Ground Point [package="Reference symbol"]
  GND12 = Ground Point [package="Reference symbol"]
  Tank_1_Sender = Marine Reed Level Sender [package="2-wire resistive, marine float sender"]
  Tank_2_Sender = Marine Reed Level Sender [package="2-wire resistive, marine float sender"]
  PWR7 = 3.3V Power Point [package="Reference symbol"]
  PWR8 = 3.3V Power Point [package="Reference symbol"]
  R1 = Resistor [tolerance=±5% resistance=100 package="0805 [SMD]"]
  R2 = Resistor [tolerance=±5% resistance=100 package="0805 [SMD]"]
  GND13 = Ground Point [package="Reference symbol"]  # not connected
  GND14 = Ground Point [package="Reference symbol"]  # not connected
  Nozzle_Temp = 10K NTC3950 Temp Probe [package="2-wire, stainless steel probe"]
  Tank_2_Temp = 10K NTC3950 Temp Probe [package="2-wire, stainless steel probe"]
  Tank_1_Temp = 10K NTC3950 Temp Probe [package="2-wire, stainless steel probe"]
  PWR9 = 3.3V Power Point [package="Reference symbol"]
  GND15 = Ground Point [package="Reference symbol"]
  R3 = Resistor [tolerance=±5% power=0.25 resistance=10k package=THT]
  R4 = Resistor [tolerance=±5% power=0.25 resistance=10k package=THT]
  R5 = Resistor [tolerance=±5% power=0.25 resistance=10k package=THT]

nets:
  N1: J1.PC5, M3.pin1
  N2: J1.E5V, M1.Pin_3
  N3: J1.GND#333, M1.Pin_4
  N4: J1.D8, Fire_Ext_Retr.+
  N5: J1.D9_PWM, SSR4.Input_+
  N6: J1.D10_PWM/SS, Raspberry_Pi1.GPIO15
  N7: J1.D2, Tank_1_Solenoids.+
  N8: J1.D3_PWM, Tank_2_Solenoids.+
  N9: J1.D4, SSR1.Input_+
  N10: J1.D5_PWM, SSR2.Input_+
  N11: J1.D6_PWM, SSR3.Input_+
  N12: J1.D7, Fire_Ext_Extnd.+
  3V3: J1.3V3, PWR1.3.3V
  N13: J1.GND#1188, GND5.GND
  N14: J1.PB2, M4.pin1
  N15: J1.PB1, M5.pin1
  N16: J1.PB7, Raspberry_Pi1.GPIO14
  GND: Raspberry_Pi1.GND, M2.Pin_4, GND10.GND
  N17: Raspberry_Pi1.5V, M2.Pin_3
  N18: M1.Pin_1, M2.Pin_1, PSU1.+12V_4
  N19: M1.Pin_2, M2.Pin_2, PSU1.GND_4
  N20: M3.pin2, M4.pin2, M5.pin2, GND11.GND
  N21: M3.pin3, M4.pin3, M5.pin3, PWR6.3.3V
  N22: M6.pin_1, SSR4.Output_-
  N23: M6.pin_2, SSR4.Output_+
  N24: Tank_2_Solenoids.S, Tank_1_Solenoids.S, Fire_Ext_Extnd.S, Fire_Ext_Retr.S, PWR5.12V
  N25: Tank_2_Solenoids.-, Tank_1_Solenoids.-, Fire_Ext_Extnd.-, Fire_Ext_Retr.-, GND9.GND
  N26: Tank_2_Solenoids.NO, Tank_2_Upper_Solenoid.pin2, Tank_2_Lower_Solenoid.pin2
  N27: Tank_1_Solenoids.Common, PSU1.+12V_1
  N28: Tank_1_Solenoids.NO, Tank_1_Upper_Solenoid.pin2, Tank_1_Lower_Solenoid.pin2
  N29: Fire_Ext_Extnd.NC, Fire_Ext_Retr.NC, PSU1.GND_3
  N30: Fire_Ext_Extnd.Common, A_______B.+
  N31: Fire_Ext_Retr.Common, F1.1
  N32: SSR1.Input_-, SSR2.Input_-, SSR3.Input_-, SSR4.Input_-, GND12.GND
  N33: SSR1.Output_+, Tank_1_Heater.pin_0
  N34: SSR1.Output_-, Tank_1_Heater.pin_1
  N35: SSR2.Output_+, Tank_2.pin_0
  N36: SSR2.Output_-, Tank_2.pin_1
  N37: SSR3.Output_+, Nozzle_Heater.pin_0
  N38: SSR3.Output_-, Nozzle_Heater.pin_1
  N39: Tank_1_Upper_Solenoid.pin1, Tank_2_Upper_Solenoid.pin1, GND2.GND
  N40: Tank_1_Lower_Solenoid.pin1, Tank_2_Lower_Solenoid.pin1, GND1.GND
  N41: PSU1.GND_1, GND3.GND
  N42: A_______B.-, F1.2
  N43: Tank_1_Sender.Signal, PWR7.3.3V
  N44: Tank_1_Sender.GND, R1.Pin_1
  N45: Tank_2_Sender.Signal, PWR8.3.3V
  N46: Tank_2_Sender.GND, R2.Pin_1
  N47: Nozzle_Temp.T1, Tank_2_Temp.T1, Tank_1_Temp.T1, PWR9.3.3V
  N48: Nozzle_Temp.T2, R5.Pin_0
  N49: Tank_2_Temp.T2, R4.Pin_0
  N50: Tank_1_Temp.T2, R3.Pin_0
  N51: GND15.GND, R3.Pin_1, R4.Pin_1, R5.Pin_1

notes:
  SSR1-SSR3 (heaters) are drawn as SSR-40DD but have been swapped out for SSR-40DA (3-32V DC in, 24-380V AC out).
  The DD has a DC output and cannot switch the 120V AC heaters. Same pins and wiring; the part graphic was not changed.
  The four tank solenoids (Tank 1/2 Upper/Lower) have been swapped out for U.S. Solid 1/4" motorized ball valves (normally closed, 9-24V, 2-wire auto return).
  The solenoids stuck and overheated on dirty oil. Same relays and 12V wiring; the part graphic was not changed.

custom parts:
  KY-019 5V Relay Module: KY-019 5V Relay module, used to control AC circuits. (Special thanks to vanepp for fixing the PCB holes and other errors)
  SSR-40DD Solid State Relay (40A, w/ Heatsink): Custom part for the SSR-40DD DC-input / DC-output solid state relay mounted on an aluminum heatsink, used to switch the block heaters in the WVO/WMO refinery. No official Fritzing part exists for this exact module; this is a simplified representation (not photorealistic) with correctly labeled input/output screw terminals.
  12V Power Supply (4x + / 4x -): Generic 12V DC power supply unit with 4 positive output terminals and 4 negative/ground output terminals, for distributing 12V to multiple solenoid valves, relays, or other loads in the WVO/WMO refinery build. Simplified representation, not photorealistic.
  Ground Point: Single-pin ground reference point, with a real graphic in breadboard view (unlike Fritzing's built-in Ground symbol, which is schematic-only). Use to mark a common ground point in a physical wiring layout without drawing a wire; label matches the ground symbol used in the schematic.
  Linear Actuator (2-wire DC): Generic 2-wire DC linear actuator. Extends/retracts by reversing motor polarity, so it needs to be driven through an H-bridge or DPDT relay rather than a simple on/off relay. Simplified representation, not photorealistic.
  3.3V Power Point: Single-pin 3.3V power reference point, with a real graphic in breadboard view (unlike Fritzing's built-in power label symbols, which are schematic-only). Use to mark a common 3.3V supply point in a physical wiring layout without drawing a wire back to the source every time.
  12V Power Point: Single-pin 12V power reference point, with a real graphic in breadboard view (unlike Fritzing's built-in power label symbols, which are schematic-only). Use to mark a common 12V supply point in a physical wiring layout without drawing a wire back to the source every time.
  Marine Reed Level Sender: Marine boat water/fuel level gauge sender, 2-wire resistive reed/float type. Resistance varies with float position along the probe (American/SAE standard: 240 ohm empty, 33 ohm full, measured on this unit). Requires an external fixed resistor to form a voltage divider; does not produce a voltage on its own. Simplified representation, not photorealistic.
  10K NTC3950 Temp Probe: 10K NTC3950 thermistor probe, stainless steel waterproof housing on a cable. Not polarized, either lead can go to either side of a divider. Requires an external fixed resistor (10k recommended, matches R25) to form a voltage divider; does not produce a voltage on its own. Simplified representation, not photorealistic.
