# Fritzing sketch Untitled Sketch 3 (saved by Fritzing 1.0.1rc)

parts:
  R1 = Resistor [tolerance=±5% power=0.25 resistance=10k package=THT]
  PWR1 = 3.3V Power Point [package="Reference symbol"]
  Temp_sensor = POT [knob_status=50% package=trim_pot]
  GND1 = Ground Point [package="Reference symbol"]  # not connected
  STM32_PA0 = AD654 - Low Cost Monolithic Voltage-to-Frequency Converter [part_number=AD654]  # not connected

nets:
  N1: R1.Pin_0, Temp_sensor.A
  N2: PWR1.3.3V, Temp_sensor.S

custom parts:
  3.3V Power Point: Single-pin 3.3V power reference point, with a real graphic in breadboard view (unlike Fritzing's built-in power label symbols, which are schematic-only). Use to mark a common 3.3V supply point in a physical wiring layout without drawing a wire back to the source every time.
  Ground Point: Single-pin ground reference point, with a real graphic in breadboard view (unlike Fritzing's built-in Ground symbol, which is schematic-only). Use to mark a common ground point in a physical wiring layout without drawing a wire; label matches the ground symbol used in the schematic.
